# Fritzing sketch uart (saved by Fritzing 0.9.3b)

parts:
  U1 = ESP8266 WiFi Module [part_number=ESP8266]
  USBUART1 = PL2303 USB UART Breakout

nets:
  N1: U1.RXD, USBUART1.TXD
  N2: U1.CH_PD, USBUART1.VCCIO
  GND: U1.GND, USBUART1.GND
  N3: U1.TXD, USBUART1.RXD

custom parts:
  ESP8266 WiFi Module: Generic WiFi Module based on the ESP8266 with onboard PCB antenna and UART communications
  PL2303 USB UART Breakout: PL2302 Usb Uart Breakout Board with Battery
